// Logisim project 9999 ripple count.circ as structural Verilog: 3 circuits, main circuit main
module main (
  input  Reset,
  input  Set,
  input  in_3,
  input  in_4,
  input  in_5,
  input  in_6,
  input  in_7,
  input  in_8
);

  wire clock_1_out, d_ff_1_q, d_ff_2_q, d_ff_3_q, when_9_tff_1_x, when_9_tff_2_x, when_9_tff_3_x;
  wire [3:0] sync_count_only_to_9_1_out_4, sync_count_only_to_9_2_out_4, sync_count_only_to_9_3_out_4,
       sync_count_only_to_9_4_out_4;

  Clock clock_1 (.out(clock_1_out));
  Sync_count_only_to_9 sync_count_only_to_9_1 (
    .out_4(sync_count_only_to_9_1_out_4), .CLock(clock_1_out), .Set(Reset), .Reset(Set));
  when_9_Tff when_9_tff_1 (
    .Q3(sync_count_only_to_9_1_out_4[3]), .Q2(sync_count_only_to_9_1_out_4[2]),
    .Q1(sync_count_only_to_9_1_out_4[1]), .Q0(sync_count_only_to_9_1_out_4[0]), .x(when_9_tff_1_x));
  Hex_Digit_Display hex_digit_display_1 (.value(sync_count_only_to_9_4_out_4));  // open: dp
  Sync_count_only_to_9 sync_count_only_to_9_2 (
    .out_4(sync_count_only_to_9_2_out_4), .CLock(d_ff_1_q), .Set(Reset), .Reset(Set));
  D_Flip_Flop d_ff_1 (
    .clk(clock_1_out), .D(when_9_tff_1_x), .Q(d_ff_1_q), .preset(in_5), .en(1'b1), .reset(in_8));  // open: Qn
  Hex_Digit_Display hex_digit_display_2 (.value(sync_count_only_to_9_3_out_4));  // open: dp
  Hex_Digit_Display hex_digit_display_3 (.value(sync_count_only_to_9_2_out_4));  // open: dp
  Hex_Digit_Display hex_digit_display_4 (.value(sync_count_only_to_9_1_out_4));  // open: dp
  Sync_count_only_to_9 sync_count_only_to_9_3 (
    .out_4(sync_count_only_to_9_3_out_4), .CLock(d_ff_2_q), .Set(Reset), .Reset(Set));
  when_9_Tff when_9_tff_2 (
    .Q3(sync_count_only_to_9_2_out_4[3]), .Q2(sync_count_only_to_9_2_out_4[2]),
    .Q1(sync_count_only_to_9_2_out_4[1]), .Q0(sync_count_only_to_9_2_out_4[0]), .x(when_9_tff_2_x));
  D_Flip_Flop d_ff_2 (
    .clk(clock_1_out), .D(when_9_tff_2_x), .Q(d_ff_2_q), .preset(in_3), .en(1'b1), .reset(in_6));  // open: Qn
  Sync_count_only_to_9 sync_count_only_to_9_4 (
    .out_4(sync_count_only_to_9_4_out_4), .CLock(d_ff_3_q), .Set(Reset), .Reset(Set));
  when_9_Tff when_9_tff_3 (
    .Q3(sync_count_only_to_9_3_out_4[3]), .Q2(sync_count_only_to_9_3_out_4[2]),
    .Q1(sync_count_only_to_9_3_out_4[1]), .Q0(sync_count_only_to_9_3_out_4[0]), .x(when_9_tff_3_x));
  D_Flip_Flop d_ff_3 (
    .clk(clock_1_out), .D(when_9_tff_3_x), .Q(d_ff_3_q), .preset(in_4), .en(1'b1), .reset(in_7));  // open: Qn
endmodule

module when_9_Tff (
  input  Q3,
  input  Q2,
  input  Q1,
  input  Q0,
  output x
);

  wire not_1_out, not_2_out;

  not not_1 (not_1_out, Q2);
  not not_2 (not_2_out, Q1);
  and and_1 (x, Q3, not_1_out, not_2_out, Q0);
endmodule

module syc_count_to_9_build (
  input  Q3,
  input  Q2,
  input  Q1,
  input  Q0,
  output D3,
  output D2,
  output D1,
  output D0
);

  wire and_1_out, and_2_out, and_3_out, and_4_out, and_5_out, and_6_out, and_7_out, and_8_out, and_9_out,
       not_1_out, not_2_out, not_3_out, not_4_out, not_5_out, not_6_out, not_7_out, not_8_out;

  and and_1 (and_1_out, Q2, Q1, Q0);
  and and_2 (and_2_out, Q3, not_1_out);
  not not_1 (not_1_out, Q0);
  not not_2 (not_2_out, Q2);
  and and_3 (and_3_out, not_2_out, Q1, Q0);
  and and_4 (and_4_out, Q2, not_3_out);
  not not_3 (not_3_out, Q1);
  and and_5 (and_5_out, Q2, not_4_out);
  not not_4 (not_4_out, Q0);
  and and_6 (and_6_out, Q3, Q2);
  not not_5 (not_5_out, Q3);
  and and_7 (and_7_out, not_5_out, not_6_out, Q0);
  not not_6 (not_6_out, Q1);
  and and_8 (and_8_out, Q1, not_7_out);
  not not_7 (not_7_out, Q0);
  not not_8 (not_8_out, Q0);
  and and_9 (and_9_out, Q3, Q2);
  or or_1 (D3, and_1_out, and_2_out);
  or or_2 (D2, and_3_out, and_4_out, and_5_out, and_6_out);
  or or_3 (D1, and_7_out, and_8_out);
  or or_4 (D0, not_8_out, and_9_out);
endmodule
