// Logisim project Flip-Flops.circ as structural Verilog: 4 circuits, main circuit main
module main (
  input  R,
  input  S,
  output Q,
  output nQ
);

  nor nor_1 (Q, R, nQ);
  nor nor_2 (nQ, Q, S);
endmodule

module RS_FlipFlops__NAND_Latch (
  input  R,
  input  S,
  output Q,
  output nQ
);

  nand nand_1 (Q, R, nQ);
  nand nand_2 (nQ, Q, S);
endmodule

module Clocked_RS_Flip_Flops (
  input  R,
  input  S,
  output Q,
  output nQ
);

  wire and_1_out, and_2_out, clock_1_out;

  Clock clock_1 (.out(clock_1_out));
  and and_1 (and_1_out, R, clock_1_out);
  and and_2 (and_2_out, clock_1_out, S);
  nor nor_1 (Q, and_1_out, nQ);
  nor nor_2 (nQ, Q, and_2_out);
endmodule

module Clocked_D_Type_Latch (
  input  D,
  output Q,
  output nQ
);

  wire and_1_out, and_2_out, clock_1_out, not_1_out;

  not not_1 (not_1_out, D);
  Clock clock_1 (.out(clock_1_out));
  and and_1 (and_1_out, not_1_out, clock_1_out);
  and and_2 (and_2_out, clock_1_out, D);
  nor nor_1 (Q, and_1_out, nQ);
  nor nor_2 (nQ, Q, and_2_out);
endmodule
