// Logisim project 4-bit Multiplier.circ as structural Verilog: 6 circuits, main circuit main
module calc (
  input  [3:0] A,
  input  [3:0] B,
  output [3:0] out_3,
  output [3:0] out_4,
  output [3:0] out_5,
  output [3:0] out_6
);

  _2Bit_Multiplier A0B0 (.B(B[1:0]), .C(out_3), .A(A[1:0]));
  _2Bit_Multiplier B0A1 (.B(B[1:0]), .C(out_4), .A(A[3:2]));
  _2Bit_Multiplier B1A0 (.B(B[3:2]), .C(out_5), .A(A[1:0]));
  _2Bit_Multiplier B1A1 (.B(B[3:2]), .C(out_6), .A(A[3:2]));
endmodule

// 2-bit Multi
module _2Bit_Multiplier (
  input  [1:0] A,
  input  [1:0] B,
  output [3:0] C
);

  wire and_2_out, and_3_out, and_4_out, and_5_out;

  and and_1 (C[3], A[0], B[1], A[1], B[0], A[1], B[1]);
  and and_2 (and_2_out, A[0], B[1], A[1], B[0]);
  and and_3 (and_3_out, A[1], B[1]);
  and and_4 (and_4_out, A[0], B[1]);
  and and_5 (and_5_out, A[1], B[0]);
  and and_6 (C[0], A[0], B[0]);
  xor xor_1 (C[2], and_2_out, and_3_out);
  xor xor_2 (C[1], and_4_out, and_5_out);
endmodule

module main (
  input  [3:0] A,
  input  [3:0] B,
  output out_3,
  output [7:0] out_4
);

  wire [3:0] A0B0_c, B0A1_c, B1A0_c, B1A1_c, n4_bit_adder_1_s;
  wire [6:6] n4_bit_adder_1_cout;

  Hex_Digit_Display hex_digit_display_1 (.value(A));  // open: dp
  Hex_Digit_Display hex_digit_display_2 (.value(B));  // open: dp
  _2Bit_Multiplier A0B0 (.B(B[1:0]), .C(A0B0_c), .A(A[1:0]));
  _2Bit_Multiplier B0A1 (.B(B[1:0]), .C(B0A1_c), .A(A[3:2]));
  _2Bit_Multiplier B1A0 (.B(B[3:2]), .C(B1A0_c), .A(A[1:0]));
  _2Bit_Multiplier B1A1 (.B(B[3:2]), .C(B1A1_c), .A(A[3:2]));
  _4_bit_adder u_4_bit_adder_1 (
    .in_1(B0A1_c), .in_2(1'b0), .in_3(B1A0_c), .Cout(n4_bit_adder_1_cout[6]), .S(n4_bit_adder_1_s));
  _8_bit_adder u_8_bit_adder_1 (
    .in_1({B1A1_c, A0B0_c}), .in_2(1'b0), .in_3({1'b0, n4_bit_adder_1_cout[6], n4_bit_adder_1_s, 2'b00}),
    .out_4(out_3), .out_5(out_4));
  Hex_Digit_Display hex_digit_display_3 (.value(out_4[7:4]));  // open: dp
  Hex_Digit_Display hex_digit_display_4 (.value(out_4[3:0]));  // open: dp

  // Notes on the sheet:
  //   1) Find the multiplication
  //   2) Add the middle
  //   3) Add it all
endmodule

module _4_bit_adder (
  input  [3:0] in_1,
  input  in_2,
  input  [3:0] in_3,
  output Cout,
  output [3:0] S
);

  wire full_adder_1_cout, full_adder_2_cout, full_adder_3_cout;

  Full_Adder full_adder_1 (.Cin(in_2), .A(in_1[0]), .B(in_3[0]), .Cout(full_adder_1_cout), .S(S[0]));
  Full_Adder full_adder_2 (.Cin(full_adder_1_cout), .A(in_1[1]), .B(in_3[1]), .Cout(full_adder_2_cout), .S(S[1]));
  Full_Adder full_adder_3 (.Cin(full_adder_2_cout), .A(in_1[2]), .B(in_3[2]), .Cout(full_adder_3_cout), .S(S[2]));
  Full_Adder full_adder_4 (.Cin(full_adder_3_cout), .A(in_1[3]), .B(in_3[3]), .Cout(Cout), .S(S[3]));
endmodule

module _8_bit_adder (
  input  [7:0] in_1,
  input  in_2,
  input  [7:0] in_3,
  output out_4,
  output [7:0] out_5
);

  wire n4_bit_adder_1_cout;

  _4_bit_adder u_4_bit_adder_1 (
    .in_1(in_1[3:0]), .in_2(in_2), .in_3(in_3[3:0]), .Cout(n4_bit_adder_1_cout), .S(out_5[3:0]));
  _4_bit_adder u_4_bit_adder_2 (
    .in_1(in_1[7:4]), .in_2(n4_bit_adder_1_cout), .in_3(in_3[7:4]), .Cout(out_4), .S(out_5[7:4]));
endmodule

module Full_Adder (
  input  Cin,
  input  A,
  input  B,
  output Cout,
  output S
);

  wire and_1_out, and_2_out, and_3_out, and_4_out, and_5_out, and_6_out, and_7_out, not_1_out, not_2_out,
       not_3_out, not_4_out, not_5_out, not_6_out;

  not not_1 (not_1_out, Cin);
  not not_2 (not_2_out, A);
  not not_3 (not_3_out, Cin);
  not not_4 (not_4_out, B);
  not not_5 (not_5_out, A);
  not not_6 (not_6_out, B);
  and and_1 (and_1_out, A, B);
  or or_1 (Cout, and_1_out, and_2_out, and_3_out);
  and and_2 (and_2_out, Cin, B);
  and and_3 (and_3_out, Cin, A);
  and and_4 (and_4_out, not_1_out, not_2_out, B);
  and and_5 (and_5_out, not_3_out, A, not_4_out);
  and and_6 (and_6_out, Cin, not_5_out, not_6_out);
  and and_7 (and_7_out, Cin, A, B);
  or or_2 (S, and_4_out, and_5_out, and_6_out, and_7_out);
endmodule
