// Logisim project 9999 ripple count.circ as structural Verilog: 4 circuits, main circuit main
module main (
  input  Set,
  input  Reset,
  input  in_3,
  input  in_4,
  input  in_5,
  input  in_6,
  input  in_7,
  input  in_8
);

  wire clock_1_out, d_ff_1_q, d_ff_2_q, d_ff_3_q, when_9_tff_1_x, when_9_tff_2_x, when_9_tff_3_x;
  wire [3:0] syc_count_flip_flop_1_out_4, syc_count_flip_flop_2_out_4, syc_count_flip_flop_3_out_4,
       syc_count_flip_flop_4_out_4;

  Clock clock_1 (.out(clock_1_out));
  syc_count_flip_flop syc_count_flip_flop_1 (
    .out_4(syc_count_flip_flop_1_out_4), .CLock(clock_1_out), .Set(Set), .Reset(Reset));
  when_9_Tff when_9_tff_1 (
    .Q3(syc_count_flip_flop_1_out_4[3]), .Q2(syc_count_flip_flop_1_out_4[2]),
    .Q1(syc_count_flip_flop_1_out_4[1]), .Q0(syc_count_flip_flop_1_out_4[0]), .x(when_9_tff_1_x));
  Hex_Digit_Display hex_digit_display_1 (.value(syc_count_flip_flop_4_out_4));  // open: dp
  syc_count_flip_flop syc_count_flip_flop_2 (
    .out_4(syc_count_flip_flop_2_out_4), .CLock(d_ff_1_q), .Set(Set), .Reset(Reset));
  D_Flip_Flop d_ff_1 (
    .clk(clock_1_out), .D(when_9_tff_1_x), .Q(d_ff_1_q), .preset(in_5), .en(1'b1), .reset(in_8));  // open: Qn
  Hex_Digit_Display hex_digit_display_2 (.value(syc_count_flip_flop_3_out_4));  // open: dp
  Hex_Digit_Display hex_digit_display_3 (.value(syc_count_flip_flop_2_out_4));  // open: dp
  Hex_Digit_Display hex_digit_display_4 (.value(syc_count_flip_flop_1_out_4));  // open: dp
  syc_count_flip_flop syc_count_flip_flop_3 (
    .out_4(syc_count_flip_flop_3_out_4), .CLock(d_ff_2_q), .Set(Set), .Reset(Reset));
  when_9_Tff when_9_tff_2 (
    .Q3(syc_count_flip_flop_2_out_4[3]), .Q2(syc_count_flip_flop_2_out_4[2]),
    .Q1(syc_count_flip_flop_2_out_4[1]), .Q0(syc_count_flip_flop_2_out_4[0]), .x(when_9_tff_2_x));
  D_Flip_Flop d_ff_2 (
    .clk(clock_1_out), .D(when_9_tff_2_x), .Q(d_ff_2_q), .preset(in_3), .en(1'b1), .reset(in_6));  // open: Qn
  syc_count_flip_flop syc_count_flip_flop_4 (
    .out_4(syc_count_flip_flop_4_out_4), .CLock(d_ff_3_q), .Set(Set), .Reset(Reset));
  when_9_Tff when_9_tff_3 (
    .Q3(syc_count_flip_flop_3_out_4[3]), .Q2(syc_count_flip_flop_3_out_4[2]),
    .Q1(syc_count_flip_flop_3_out_4[1]), .Q0(syc_count_flip_flop_3_out_4[0]), .x(when_9_tff_3_x));
  D_Flip_Flop d_ff_3 (
    .clk(clock_1_out), .D(when_9_tff_3_x), .Q(d_ff_3_q), .preset(in_4), .en(1'b1), .reset(in_7));  // open: Qn
endmodule

module when_9_Tff (
  input  Q3,
  input  Q2,
  input  Q1,
  input  Q0,
  output x
);

  wire not_1_out, not_2_out;

  not not_1 (not_1_out, Q2);
  not not_2 (not_2_out, Q1);
  and and_1 (x, Q3, not_1_out, not_2_out, Q0);
endmodule

module syc_count_to_9 (
  input  Q3,
  input  Q2,
  input  Q1,
  input  Q0,
  output D3,
  output D2,
  output D1,
  output D0
);

  wire and_1_out, and_2_out, and_3_out, and_4_out, and_5_out, and_6_out, and_7_out, and_8_out, and_9_out,
       not_1_out, not_2_out, not_3_out, not_4_out, not_5_out, not_6_out, not_7_out, not_8_out, not_9_out,
       not_10_out, not_11_out, not_12_out, not_13_out, not_14_out, not_15_out, not_16_out, not_17_out,
       not_18_out, not_19_out;

  not not_1 (not_1_out, Q3);
  not not_2 (not_2_out, Q2);
  not not_3 (not_3_out, Q1);
  not not_4 (not_4_out, Q0);
  not not_5 (not_5_out, Q3);
  not not_6 (not_6_out, Q2);
  not not_7 (not_7_out, Q3);
  not not_8 (not_8_out, Q1);
  not not_9 (not_9_out, Q3);
  not not_10 (not_10_out, Q0);
  not not_11 (not_11_out, Q3);
  not not_12 (not_12_out, Q1);
  and and_1 (and_1_out, not_11_out, not_12_out, Q0);
  not not_13 (not_13_out, Q3);
  and and_2 (and_2_out, not_13_out, Q1, not_14_out);
  not not_14 (not_14_out, Q0);
  not not_15 (not_15_out, Q3);
  and and_3 (and_3_out, not_15_out, not_16_out);
  not not_16 (not_16_out, Q0);
  not not_17 (not_17_out, Q2);
  not not_18 (not_18_out, Q1);
  and and_4 (and_4_out, not_17_out, not_18_out, not_19_out);
  not not_19 (not_19_out, Q0);
  and and_5 (and_5_out, not_1_out, Q2, Q1, Q0);
  or or_1 (D3, and_5_out, and_6_out);
  and and_6 (and_6_out, Q3, not_2_out, not_3_out, not_4_out);
  and and_7 (and_7_out, not_5_out, not_6_out, Q1, Q0);
  and and_8 (and_8_out, not_7_out, Q2, not_8_out);
  or or_2 (D2, and_7_out, and_8_out, and_9_out);
  and and_9 (and_9_out, not_9_out, Q2, not_10_out);
  or or_3 (D1, and_1_out, and_2_out);
  or or_4 (D0, and_3_out, and_4_out);
endmodule

module syc_count_flip_flop (
  input  Reset,
  input  Set,
  input  CLock,
  output [3:0] out_4
);

  wire d_ff_1_q, d_ff_2_q, d_ff_3_q, d_ff_4_q;

  D_Flip_Flop d_ff_1 (.clk(CLock), .D(out_4[3]), .Q(d_ff_1_q), .preset(Reset), .en(1'b1), .reset(Set));  // open: Qn
  D_Flip_Flop d_ff_2 (.clk(CLock), .D(out_4[2]), .Q(d_ff_2_q), .preset(Reset), .en(1'b1), .reset(Set));  // open: Qn
  D_Flip_Flop d_ff_3 (.clk(CLock), .D(out_4[1]), .Q(d_ff_3_q), .preset(Reset), .en(1'b1), .reset(Set));  // open: Qn
  D_Flip_Flop d_ff_4 (.clk(CLock), .D(out_4[0]), .Q(d_ff_4_q), .preset(Reset), .en(1'b1), .reset(Set));  // open: Qn
  syc_count_to_9 syc_count_to_9_1 (
    .Q3(d_ff_1_q), .Q2(d_ff_2_q), .Q1(d_ff_3_q), .Q0(d_ff_4_q), .D3(out_4[3]), .D2(out_4[2]), .D1(out_4[1]),
    .D0(out_4[0]));
  Hex_Digit_Display hex_digit_display_1 (.value(out_4));  // open: dp
endmodule
